# Fritzing sketch C64NeoMonitor R1 (saved by Fritzing 0.9.3b)
circuit board: 6.13021cm x 3.5687cm
breadboards: 1

parts:
  Trinket = Adafruit Trinket 5V
  IC1 = IC, DIP package, 14 pins [chip_label=IC]
  C64 = female pin header, 4 pins [form="♀ (female)"]
  Pixels = female pin header, 4 pins [form="♀ (female)"]
  PWR = female pin header, 2 pins [form="♀ (female)"]

nets:
  GND: Trinket.GND, IC1.pin7, Pixels.pin1, Pixels.pin4, PWR.pin2
  N1: Trinket.#0, Pixels.pin3
  5V: Trinket.+5V, IC1.pin14, Pixels.pin2, PWR.pin1
  N2: IC1.pin1, C64.pin1
  1Y: IC1.pin2
  N3: IC1.pin3, C64.pin2
  N4: IC1.pin5, C64.pin3
  N5: IC1.pin9, C64.pin4

notes:
  Trinket
  74LS04
  5V
  GND
  IRQ
  ROM
  GAM
  NMI
  DIN

custom parts:
  Adafruit Trinket 5V: Trinket may be small, but do not be fooled by its size! It's a tiny microcontroller board, built around the Atmel ATtiny85, a little chip with a lot of power. We wanted to design a microcontroller board that was small enough to fit into any project, and low cost enough to use without hesitation. Perfect for when you don't want to give up your expensive dev-board and you aren't willing to take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
