# Fritzing sketch C64NeoMonitor R6 (saved by Fritzing 0.9.3b)
circuit board: 4.8947cm x 2.44608cm
breadboards: 1

parts:
  Trinket = Adafruit Trinket 5V
  IC1 = IC, DIP package, 14 pins [chip_label=IC]
  C64 = female pin header, 4 pins [form="♀ (female)"]
  Pixels = female pin header, 4 pins [form="♀ (female)"]
  PWR = female pin header, 2 pins [form="♀ (female)"]
  Pad4 = Pad [width=1.6141896328502452 height=2.0137205893719807 connect=center]  # not connected
  Pad5 = Pad [width=1.6141896328502452 height=2.0137205893719807 connect=center]  # not connected
  Pad6 = Pad [width=1.6141896328502452 height=2.0137205893719807 connect=center]  # not connected
  Pad7 = Pad [width=1.6141896328502452 height=2.0137205893719807 connect=center]  # not connected
  Pad8 = Pad [width=2.1709314871794816 height=0.56444357606837925 connect=center]  # not connected
  Pad9 = Pad [width=2.1709314871794816 height=0.56444357606837925 connect=center]  # not connected
  R1 = Resistor [tolerance=±5% resistance=300 package=THT]

nets:
  GND: Trinket.GND, IC1.pin7, Pixels.pin1, Pixels.pin4, PWR.pin2
  1Y: Trinket.#1, IC1.pin2
  2Y: Trinket.#2, IC1.pin4
  N1: Trinket.#0, R1.Pin_0
  4Y: Trinket.#4, IC1.pin8
  3Y: Trinket.#3, IC1.pin6
  5V: Trinket.+5V, IC1.pin14, Pixels.pin2, PWR.pin1
  N2: IC1.pin1, C64.pin1
  N3: IC1.pin3, C64.pin2
  N4: IC1.pin5, C64.pin3
  N5: IC1.pin9, C64.pin4
  N6: Pixels.pin3, R1.Pin_1

notes:
  Trinket 5V
  74LS04
  5V
  GND
  IRQ
  ROM
  GAM
  NMI
  DIN
  C64 NeoPixel Monitor
  Leif Bloomquist
  2018 0v1
  R1

custom parts:
  Adafruit Trinket 5V: Trinket may be small, but do not be fooled by its size! It's a tiny microcontroller board, built around the Atmel ATtiny85, a little chip with a lot of power. We wanted to design a microcontroller board that was small enough to fit into any project, and low cost enough to use without hesitation. Perfect for when you don't want to give up your expensive dev-board and you aren't willing to take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
